// Digital circuit TBOS Testing.dig as structural Verilog
module TBOS_Testing (
  input  clk
);

  wire button_1_out, button_2_out, button_3_out, telescope_computing_system_1_os_running;
  wire [15:0] Drive_1_d, Drive_2_d, Keyboard_0_d, Root_Drive_d, TBOS_1_0_d,
       telescope_computing_system_1_os_adr, telescope_computing_system_1_status_code,
       telescope_computing_system_1_tk1_out;
  wire [16:16] Keyboard_0_av;
  wire [18:16] telescope_computing_system_1_tk1_out_2;
  wire [19:0] telescope_computing_system_1_tnet_o_1, telescope_computing_system_1_tnet_o_2;
  wire [33:0] telescope_computing_system_1_d0_out, telescope_computing_system_1_d1_out,
       telescope_computing_system_1_d2_out;

  LED OS_Is_Running (.in(telescope_computing_system_1_os_running));
  // Probe Status on telescope_computing_system_1_status_code
  Telescope_Computing_System telescope_computing_system_1 (
    .OS_Running(telescope_computing_system_1_os_running),
    .Status_Code(telescope_computing_system_1_status_code), .Power_On(button_1_out), .Clock_Input(clk),
    .Pause(button_2_out), .Pause_Mode(1'b1), .STOP(button_3_out),
    .OS_Adr(telescope_computing_system_1_os_adr), .OS_In(TBOS_1_0_d), .D0_In(Root_Drive_d),
    .D0_Out(telescope_computing_system_1_d0_out), .D1_In(Drive_1_d),
    .D1_Out(telescope_computing_system_1_d1_out), .D2_In(Drive_2_d),
    .D2_Out(telescope_computing_system_1_d2_out), .D3_In({16{1'b0}}), .TNET_I_0({20{1'b0}}),
    .TNET_O_1(telescope_computing_system_1_tnet_o_1), .TNET_I_1(telescope_computing_system_1_tnet_o_1),
    .TNET_O_2(telescope_computing_system_1_tnet_o_2), .TNET_I_2(telescope_computing_system_1_tnet_o_2),
    .TNET_I_3({20{1'b0}}), .K0_In({17{1'b0}}),
    .TK1_Out({telescope_computing_system_1_tk1_out_2, telescope_computing_system_1_tk1_out}),
    .K1_In({Keyboard_0_av[16], Keyboard_0_d}), .K2_In({17{1'b0}}), .K3_In({17{1'b0}}), .GPI_0({18{1'b0}}),
    .GPI_1({18{1'b0}}), .GPI_2({18{1'b0}}), .GPI_3({18{1'b0}}));  // open: D3_Out, TNET_O_0, TNET_O_3, TK0_Out, TK2_Out, TK3_Out, GPO_0, GPO_1, GPO_2, GPO_3
  Button button_1 (.out(button_1_out));
  Button button_2 (.out(button_2_out));
  Button button_3 (.out(button_3_out));
  Keyboard Keyboard_0 (
    .C(telescope_computing_system_1_tk1_out_2[18]), .en(telescope_computing_system_1_tk1_out_2[16]),
    .D(Keyboard_0_d), .av(Keyboard_0_av[16]));
  Terminal terminal_1 (
    .D(telescope_computing_system_1_tk1_out), .C(telescope_computing_system_1_tk1_out_2[18]),
    .en(telescope_computing_system_1_tk1_out_2[17]));
  // Probe OS Boot Drive Address on telescope_computing_system_1_os_adr
  ROM #(.AddrBits(16), .Bits(16)) TBOS_1_0 (.A(telescope_computing_system_1_os_adr), .sel(1'b1), .D(TBOS_1_0_d));
  EEPROMDualPort #(.AddrBits(16), .Bits(16)) Root_Drive (
    .A(telescope_computing_system_1_d0_out[31:16]), .Din(telescope_computing_system_1_d0_out[15:0]),
    .str(telescope_computing_system_1_d0_out[32]), .C(telescope_computing_system_1_d0_out[33]), .ld(1'b1),
    .D(Root_Drive_d));
  EEPROMDualPort #(.AddrBits(16), .Bits(16)) Drive_1 (
    .A(telescope_computing_system_1_d1_out[31:16]), .Din(telescope_computing_system_1_d1_out[15:0]),
    .str(telescope_computing_system_1_d1_out[32]), .C(telescope_computing_system_1_d1_out[33]), .ld(1'b1),
    .D(Drive_1_d));
  EEPROMDualPort #(.AddrBits(16), .Bits(16)) Drive_2 (
    .A(telescope_computing_system_1_d2_out[31:16]), .Din(telescope_computing_system_1_d2_out[15:0]),
    .str(telescope_computing_system_1_d2_out[32]), .C(telescope_computing_system_1_d2_out[33]), .ld(1'b1),
    .D(Drive_2_d));

  // Notes on the sheet:
  //   clk: Hz: 4096
  //   contents of TBOS_1_0 (hex, n*v repeats v):
  //   4600,f,48,65,6c,6c,6f,20,57,6f,72,6c,64,21,ffff,50a0,4800,b100
  //   ,b010,6020,2,cb21,4000,1c,3092,9901,4600,13
  //   contents of Root_Drive (hex, n*v repeats v):
  //   d,4600,2,50a0,800,2000,50a0,1000,2000,50a0,9000,4d00,a
  //   contents of Drive_1 (hex, n*v repeats v):
  //   18,4600,2,5010,24,50a0,4800,4d00,6,3009,cb01,4000,13,50a0,8800
  //   ,3090,4c00,f,4600,4,50a0,9000,3090,4600,16
  //   contents of Drive_2 (hex, n*v repeats v):
  //   c,4600,2,50a0,8800,4d00,4,3009,50a0,4800,3090,4600,2
endmodule
